# Fritzing sketch Glove Receiver Autorouted Manual Fix MCP Pins Fixed 21 (saved by Fritzing 0.9.2b)
circuit board: 5.30097cm x 2.5318cm
breadboards: 1

parts:
  74LS05 = IC, DIP package, 14 pins [chip_label=74LS05]
  5 = Header 1 [package=luxeon-pad]  # not connected
  4 = Header 1 [package=luxeon-pad]
  3 = Header 1 [package=luxeon-pad]
  2 = Header 1 [package=luxeon-pad]
  1 = Header 1 [package=luxeon-pad]
  9 = Header 1 [package=luxeon-pad]  # not connected
  8 = Header 1 [package=luxeon-pad]
  7 = Header 1 [package=luxeon-pad]
  6 = Header 1 [package=luxeon-pad]
  XBee = XBEE-1 [package=xbee-silk]
  Power = smd LED [color="Green (565nm)" package="1206 [SMD]"]
  Signal = smd LED [color="Blue (430nm)" package="1206 [SMD]"]
  Up = smd LED [color="Yellow (592nm)" package="1206 [SMD]"]
  Left = smd LED [color="Yellow (585nm)" package="1206 [SMD]"]
  Down = smd LED [color="Yellow (585nm)" package="1206 [SMD]"]
  Fire = smd LED [color="Red (635nm)" package="1206 [SMD]"]
  Right = smd LED [color="Yellow (585nm)" package="1206 [SMD]"]
  R1 = Resistor [tolerance=±5% resistance=330 package="1206 [SMD]"]
  R2 = Resistor [tolerance=±5% resistance=330 package="1206 [SMD]"]
  R3 = Resistor [tolerance=±5% resistance=330 package="1206 [SMD]"]
  R4 = Resistor [tolerance=±5% resistance=330 package="1206 [SMD]"]
  R5 = Resistor [tolerance=±5% resistance=330 package="1206 [SMD]"]
  R6 = Resistor [tolerance=±5% resistance=330 package="1206 [SMD]"]
  R7 = Resistor [tolerance=±5% resistance=330 package="1206 [SMD]"]
  U1 = PNP-Transistor [part_number=MCP1700-33 package="TO92 [THT]"]

nets:
  XBEE_UP: 74LS05.pin1, XBee.DIO2
  UP: 74LS05.pin2, 1.1, Up.cathode
  XBEE_DOWN: 74LS05.pin3, XBee.DIO4
  DOWN: 74LS05.pin4, 2.1, Down.cathode
  XBEE_LEFT: 74LS05.pin5, XBee.DIO11
  LEFT: 74LS05.pin6, 3.1, Left.cathode
  GND: 74LS05.pin7, 8.1, XBee.GND, Power.cathode, U1.E
  RIGHT: 74LS05.pin8, 4.1, Right.cathode
  XBEE_RIGHT: 74LS05.pin9, XBee.DIO12
  FIRE: 74LS05.pin12, 6.1, Fire.cathode
  XBEE_FIRE: 74LS05.pin13, XBee.DIO0
  5V: 74LS05.pin14, 7.1, R1.Pin_0, R2.Pin_0, R3.Pin_0, R4.Pin_0, R5.Pin_0, R6.Pin_0, R7.Pin_0, U1.B
  3.3V: XBee.VDD, U1.C
  RSSI: XBee.RSSI, Signal.cathode
  N1: Power.anode, R1.Pin_1
  N2: Signal.anode, R2.Pin_1
  N3: Up.anode, R3.Pin_1
  N4: Left.anode, R5.Pin_1
  N5: Down.anode, R4.Pin_1
  N6: Fire.anode, R7.Pin_1
  N7: Right.anode, R6.Pin_1

notes:
  1=Up
  2=Down
  3=Left
  4=Right
  5=PotY
  6=Fire
  7=5V
  8=GND
  9=PotX
  XBee/Retro Computer
  Joystick Interface
  Leif Bloomquist
  2015 0v2
  Note pinout swapped!
  See MCP-1700 Datasheet
